# Fritzing sketch IRLibrary (saved by Fritzing 0.9.3b)

parts:
  Q1 = NPN-Transistor [package="TO92 [THT]"]
  Part1 = Arduino Uno (Rev3)
  R1 = Resistor [tolerance=±5% resistance=470 package=THT]
  IR1 = TSOP312.., 314.. [package=THT]
  D1 = LTE-302 [package=lte-302]
  LED1 = RGB LED (com. anode, rbg) [package="5 mm [THT]"]

nets:
  GND: Q1.E, Part1.GND, IR1.GND
  N1: Q1.B, R1.Pin_1
  N2: Q1.C, D1.C
  N3: Part1.D8, LED1.green_cathode
  N4: Part1.D9_PWM, LED1.blue_cathode
  N5: Part1.D10_PWM/SS, LED1.common_anode
  N6: Part1.D11_PWM/MOSI, LED1.red_cathode
  N7: Part1.D2, IR1.Data
  N8: Part1.D3_PWM, R1.Pin_0
  N9: Part1.5V, IR1.Vs, D1.A
